# Fritzing sketch esquema (saved by Fritzing 0.8.7b)

parts:
  GY-NEO6MV3 = SUP500F [package=sup500f]
  GY2 = MPU-6050 Board GY-521 [form="♀ (female)" package=THT]
  S1 = SWITCH-MOMENTARY-2 [package=tactile_switch_smd-2]
  WeMos_D1_Mini2 = WeMos D1 Mini
  J1 = Piezo Speaker
  LED1 = smd LED [color="Red (633nm)" package="0805 [SMD]"]

nets:
  N1: GY-NEO6MV3.TX-O, WeMos_D1_Mini2.RX
  GND: GY-NEO6MV3.GND, GY2.pin2, S1.1, J1.pin1
  5V: GY-NEO6MV3.VCC, GY2.pin1, WeMos_D1_Mini2.5V, LED1.cathode
  N2: GY2.pin3, WeMos_D1_Mini2.D1
  N3: GY2.pin4, WeMos_D1_Mini2.D2
  N4: S1.2, WeMos_D1_Mini2.D6
  N5: WeMos_D1_Mini2.D3, J1.pin2
  N6: WeMos_D1_Mini2.D4, LED1.anode

custom parts:
  MPU-6050 Board GY-521: Acelerometro y Giroscopio MPU-6050 Board GY-521
